// Logisim project e2396273.circ as structural Verilog: 1 circuit, main circuit main
module main (
  input  O2,
  input  O1,
  input  O0,
  input  A1,
  input  A0,
  input  B1,
  input  B0,
  output S,
  output L0,
  output L1,
  output L2,
  output L3,
  output L4,
  output L5,
  output L6
);

  wire and_1_out, and_2_out, and_3_out, and_4_out, and_5_out, and_6_out, and_7_out, and_8_out, and_9_out,
       and_10_out, and_11_out, and_12_out, and_13_out, and_14_out, and_15_out, and_16_out, and_17_out,
       and_18_out, and_19_out, and_20_out, and_21_out, and_22_out, and_23_out, and_24_out, and_25_out,
       and_26_out, and_27_out, and_28_out, and_29_out, and_30_out, and_31_out, and_32_out, and_33_out,
       and_34_out, and_35_out, and_36_out, and_37_out, and_38_out, and_39_out, and_40_out, and_41_out,
       and_42_out, and_43_out, and_44_out, and_45_out, and_46_out, and_47_out, and_48_out, and_49_out,
       and_50_out, and_51_out, and_52_out, and_54_out, and_55_out, n3_to_8_decoder_74138_1_p5,
       n3_to_8_decoder_74138_2_p7, n3_to_8_decoder_74138_2_p8, n3_to_8_decoder_74138_4_p8,
       n3_to_8_decoder_74138_6_p8, n3_to_8_decoder_74138_7_p8, not_1_out, not_2_out, not_3_out, not_4_out,
       not_5_out, not_6_out, not_7_out, not_8_out, not_9_out, not_10_out, not_11_out, not_12_out, not_13_out,
       not_14_out, not_16_out, not_17_out, not_18_out, not_19_out, not_22_out, not_23_out, not_24_out,
       not_25_out, not_26_out, not_28_out, not_29_out, not_30_out, not_31_out, not_32_out, not_33_out,
       not_34_out, not_36_out, not_37_out, not_38_out, not_40_out, not_41_out, not_42_out, not_43_out,
       not_44_out, not_45_out, not_46_out, or_1_out, or_2_out, or_3_out, or_4_out, or_5_out, or_6_out,
       or_7_out, or_8_out, or_9_out, or_10_out, or_11_out, or_12_out, or_13_out, or_15_out, or_16_out,
       or_17_out, or_18_out, or_19_out, or_20_out, or_21_out, or_22_out, or_23_out, or_24_out, or_25_out,
       or_26_out, or_28_out, or_29_out, or_30_out, or_31_out, or_32_out, or_34_out, xor_1_out, xor_2_out,
       xor_3_out;

  not not_1 (not_1_out, O2);
  not not_2 (not_2_out, O1);
  not not_3 (not_3_out, O0);
  not not_4 (not_4_out, A1);
  not not_5 (not_5_out, A0);
  not not_6 (not_6_out, B1);
  not not_7 (not_7_out, B0);
  xor xor_1 (xor_1_out, A1, B1);
  xor xor_2 (xor_2_out, A0, B0);
  // _3_to_8_decoder__74138 #(.Facing("east")) 3_to_8_decoder_74138_1: pin names not known; wires that end beside it: O0, O1, O2, 1'b1, n3_to_8_decoder_74138_1_p5, n3_to_8_decoder_74138_1_p5
  and and_1 (and_1_out, A1, B0);
  and and_2 (and_2_out, A0, B1);
  and and_3 (and_3_out, A1, B1);
  and and_4 (and_4_out, A0, B0);
  and and_5 (and_5_out, not_4_out, not_6_out);
  and and_6 (and_6_out, not_5_out, B1);
  and and_7 (and_7_out, not_5_out, B0);
  and and_8 (and_8_out, A1, not_6_out);
  and and_9 (and_9_out, A0, not_6_out);
  and and_10 (and_10_out, A1, not_7_out);
  and and_11 (and_11_out, A0, not_7_out);
  and and_12 (and_12_out, not_5_out, not_7_out);
  and and_13 (and_13_out, not_4_out, not_5_out);
  and and_14 (and_14_out, B1, B0);
  and and_15 (and_15_out, not_6_out, B0);
  and and_16 (and_16_out, not_4_out, B1);
  and and_17 (and_17_out, not_6_out, not_7_out);
  or or_1 (or_1_out, not_5_out, B0);
  or or_2 (or_2_out, not_4_out, B1);
  // NOT_Gate not_8 has open pins: in=open, out=not_8_out
  // NOT_Gate not_9 has open pins: in=open, out=not_9_out
  // NOT_Gate not_10 has open pins: in=open, out=not_10_out
  // NOT_Gate not_11 has open pins: in=open, out=not_11_out
  // NOT_Gate not_12 has open pins: in=open, out=not_12_out
  // NOT_Gate not_13 has open pins: in=open, out=not_13_out
  // NOT_Gate not_14 has open pins: in=open, out=not_14_out
  xor xor_3 (xor_3_out, xor_1_out, and_4_out);
  and and_18 (and_18_out, xor_1_out, and_4_out);
  not not_15 (n3_to_8_decoder_74138_1_p5, 1'b1);
  or or_3 (or_3_out, and_18_out, and_3_out);
  and and_19 (and_19_out, and_16_out, or_1_out);
  or or_4 (or_4_out, and_17_out, and_9_out);
  or or_5 (or_5_out, and_17_out, and_10_out);
  and and_20 (and_20_out, or_4_out, A1);
  or or_6 (or_6_out, and_6_out, and_14_out);
  or or_7 (or_7_out, and_19_out, and_20_out);
  and and_21 (and_21_out, or_5_out, A0);
  and and_22 (and_22_out, and_13_out, B0);
  or or_8 (or_8_out, and_6_out, and_4_out);
  or or_9 (or_9_out, and_2_out, and_1_out);
  or or_10 (or_10_out, or_6_out, not_4_out);
  or or_11 (or_11_out, and_7_out, and_11_out);
  or or_12 (or_12_out, and_16_out, and_8_out);
  or or_13 (or_13_out, and_4_out, B1);
  or or_14 (S, and_21_out, and_8_out);
  and and_23 (and_23_out, or_13_out, A1);
  and and_24 (and_24_out, and_4_out, or_2_out);
  // _3_to_8_decoder__74138 #(.Facing("east")) 3_to_8_decoder_74138_2: pin names not known; wires that end beside it: xor_2_out, xor_3_out, or_3_out, 1'b1, n3_to_8_decoder_74138_1_p5, n3_to_8_decoder_74138_1_p5, n3_to_8_decoder_74138_2_p7, n3_to_8_decoder_74138_2_p8
  // _3_to_8_decoder__74138 #(.Facing("east")) 3_to_8_decoder_74138_3: pin names not known; wires that end beside it: xor_2_out, or_7_out, n3_to_8_decoder_74138_1_p5, 1'b1, n3_to_8_decoder_74138_1_p5, n3_to_8_decoder_74138_1_p5
  // _3_to_8_decoder__74138 #(.Facing("east")) 3_to_8_decoder_74138_4: pin names not known; wires that end beside it: and_22_out, or_8_out, or_9_out, 1'b1, n3_to_8_decoder_74138_1_p5, n3_to_8_decoder_74138_1_p5, n3_to_8_decoder_74138_1_p5, n3_to_8_decoder_74138_4_p8
  // _3_to_8_decoder__74138 #(.Facing("east")) 3_to_8_decoder_74138_5: pin names not known; wires that end beside it: or_10_out, n3_to_8_decoder_74138_1_p5, n3_to_8_decoder_74138_1_p5, 1'b1, n3_to_8_decoder_74138_1_p5, n3_to_8_decoder_74138_1_p5
  // _3_to_8_decoder__74138 #(.Facing("east")) 3_to_8_decoder_74138_6: pin names not known; wires that end beside it: or_11_out, or_12_out, n3_to_8_decoder_74138_1_p5, 1'b1, n3_to_8_decoder_74138_1_p5, n3_to_8_decoder_74138_1_p5, n3_to_8_decoder_74138_1_p5, n3_to_8_decoder_74138_6_p8
  // _3_to_8_decoder__74138 #(.Facing("east")) 3_to_8_decoder_74138_7: pin names not known; wires that end beside it: and_24_out, and_23_out, n3_to_8_decoder_74138_1_p5, 1'b1, 1'b1, n3_to_8_decoder_74138_1_p5, n3_to_8_decoder_74138_1_p5, n3_to_8_decoder_74138_7_p8
  // _3_to_8_decoder__74138 #(.Facing("east")) 3_to_8_decoder_74138_8: pin names not known; wires that end beside it: 1'b1, n3_to_8_decoder_74138_1_p5, and_12_out, and_5_out, n3_to_8_decoder_74138_1_p5, 1'b1, n3_to_8_decoder_74138_1_p5, 1'b1, n3_to_8_decoder_74138_1_p5, n3_to_8_decoder_74138_1_p5
  // NOT_Gate not_16 has open pins: in=open, out=not_16_out
  // NOT_Gate not_17 has open pins: in=open, out=not_17_out
  // NOT_Gate not_18 has open pins: in=open, out=not_18_out
  // NOT_Gate not_19 has open pins: in=open, out=not_19_out
  // NOT_Gate not_20 has open pins: in=open, out=n3_to_8_decoder_74138_2_p7
  // NOT_Gate not_21 has open pins: in=open, out=n3_to_8_decoder_74138_2_p8
  // NOT_Gate not_22 has open pins: in=open, out=not_22_out
  // NOT_Gate not_23 has open pins: in=open, out=not_23_out
  // NOT_Gate not_24 has open pins: in=open, out=not_24_out
  // NOT_Gate not_25 has open pins: in=open, out=not_25_out
  // NOT_Gate not_26 has open pins: in=open, out=not_26_out
  // NOT_Gate not_27 has open pins: in=open, out=n3_to_8_decoder_74138_4_p8
  // NOT_Gate not_28 has open pins: in=open, out=not_28_out
  // NOT_Gate not_29 has open pins: in=open, out=not_29_out
  // NOT_Gate not_30 has open pins: in=open, out=not_30_out
  // NOT_Gate not_31 has open pins: in=open, out=not_31_out
  // NOT_Gate not_32 has open pins: in=open, out=not_32_out
  // NOT_Gate not_33 has open pins: in=open, out=not_33_out
  // NOT_Gate not_34 has open pins: in=open, out=not_34_out
  // NOT_Gate not_35 has open pins: in=open, out=n3_to_8_decoder_74138_6_p8
  // NOT_Gate not_36 has open pins: in=open, out=not_36_out
  // NOT_Gate not_37 has open pins: in=open, out=not_37_out
  // NOT_Gate not_38 has open pins: in=open, out=not_38_out
  // NOT_Gate not_39 has open pins: in=open, out=n3_to_8_decoder_74138_7_p8
  // NOT_Gate not_40 has open pins: in=open, out=not_40_out
  // NOT_Gate not_41 has open pins: in=open, out=not_41_out
  // NOT_Gate not_42 has open pins: in=open, out=not_42_out
  // NOT_Gate not_43 has open pins: in=open, out=not_43_out
  // NOT_Gate not_44 has open pins: in=open, out=not_44_out
  // NOT_Gate not_45 has open pins: in=open, out=not_45_out
  // NOT_Gate not_46 has open pins: in=open, out=not_46_out
  and and_25 (and_25_out, not_16_out, not_8_out);
  and and_26 (and_26_out, not_23_out, not_9_out);
  and and_27 (and_27_out, not_10_out, n3_to_8_decoder_74138_4_p8);
  and and_28 (and_28_out, not_11_out, not_33_out);
  and and_29 (and_29_out, not_12_out, n3_to_8_decoder_74138_6_p8);
  and and_30 (and_30_out, not_13_out, n3_to_8_decoder_74138_7_p8);
  and and_31 (and_31_out, not_14_out, not_43_out);
  and and_32 (and_32_out, not_17_out, not_8_out);
  and and_33 (and_33_out, not_24_out, not_9_out);
  and and_34 (and_34_out, not_10_out, not_28_out);
  and and_35 (and_35_out, not_11_out, not_34_out);
  and and_36 (and_36_out, not_12_out, not_36_out);
  and and_37 (and_37_out, not_13_out, not_40_out);
  and and_38 (and_38_out, not_14_out, not_44_out);
  and and_39 (and_39_out, not_18_out, not_8_out);
  and and_40 (and_40_out, not_25_out, not_9_out);
  and and_41 (and_41_out, not_29_out, not_10_out);
  and and_42 (and_42_out, not_37_out, not_12_out);
  and and_43 (and_43_out, not_41_out, not_13_out);
  and and_44 (and_44_out, not_45_out, not_14_out);
  and and_45 (and_45_out, not_19_out, not_8_out);
  and and_46 (and_46_out, not_9_out, not_26_out);
  and and_47 (and_47_out, not_30_out, not_10_out);
  and and_48 (and_48_out, not_38_out, not_12_out);
  and and_49 (and_49_out, not_42_out, not_13_out);
  and and_50 (and_50_out, not_46_out, not_14_out);
  and and_51 (and_51_out, n3_to_8_decoder_74138_2_p7, not_8_out);
  and and_52 (and_52_out, not_31_out, not_10_out);
  or or_15 (or_15_out, and_25_out, and_26_out);
  or or_16 (or_16_out, and_27_out, and_28_out);
  or or_17 (or_17_out, and_29_out, and_30_out);
  or or_18 (or_18_out, and_32_out, and_33_out);
  or or_19 (or_19_out, and_34_out, and_35_out);
  or or_20 (or_20_out, and_36_out, and_37_out);
  or or_21 (or_21_out, and_39_out, and_40_out);
  or or_22 (or_22_out, and_41_out, and_42_out);
  or or_23 (or_23_out, and_43_out, and_44_out);
  or or_24 (or_24_out, and_45_out, and_46_out);
  or or_25 (or_25_out, and_47_out, and_48_out);
  or or_26 (or_26_out, and_49_out, and_50_out);
  or or_27 (L4, and_51_out, and_52_out);
  and and_53 (L5, n3_to_8_decoder_74138_2_p8, not_8_out);
  and and_54 (and_54_out, not_22_out, not_8_out);
  and and_55 (and_55_out, not_32_out, not_10_out);
  or or_28 (or_28_out, or_15_out, or_16_out);
  or or_29 (or_29_out, or_17_out, and_31_out);
  or or_30 (or_30_out, or_18_out, or_19_out);
  or or_31 (or_31_out, or_20_out, and_38_out);
  or or_32 (or_32_out, or_21_out, or_22_out);
  or or_33 (L6, and_54_out, and_55_out);
  or or_34 (or_34_out, or_24_out, or_25_out);
  or or_35 (L0, or_28_out, or_29_out);
  or or_36 (L1, or_30_out, or_31_out);
  or or_37 (L2, or_32_out, or_23_out);
  or or_38 (L3, or_34_out, or_26_out);
endmodule
